// Logisim project LUT_v2.circ as structural Verilog: 4 circuits, main circuit main
module main (
  input  in_1,
  input  in_2,
  input  in_3,
  input  in_4,
  input  in_5,
  input  in_6,
  input  [7:0] in_7,
  input  [7:0] in_8,
  input  in_9,
  input  in_10,
  input  in_11,
  input  in_12,
  input  in_13,
  input  in_14,
  input  [7:0] in_15,
  input  [7:0] in_16
);

  wire [7:1] undriven, undriven_2, undriven_3, undriven_4, undriven_5, undriven_6, undriven_7, undriven_8,
       undriven_9, undriven_10, undriven_11, undriven_12;

  lut_switch lut_switch_1 (
    .in_1(in_7), .in_2({undriven_6, in_3}), .in_3({undriven_4, in_2}), .in_5({undriven_2, in_1}),
    .out_8(undriven_6[1]));  // open: in_4, in_6, in_7
  lut_switch lut_switch_2 (
    .in_1(in_15), .in_2({undriven_5, in_11}), .in_3({undriven_3, in_10}), .in_5({undriven, in_9}),
    .out_8(undriven_5[1]));  // open: in_4, in_6, in_7
  lut_switch lut_switch_3 (
    .in_1(in_8), .in_2({undriven_12, in_6}), .in_3({undriven_10, in_5}), .in_5({undriven_8, in_4}),
    .out_8(undriven_12[1]));  // open: in_4, in_6, in_7
  lut_switch lut_switch_4 (
    .in_1(in_16), .in_2({undriven_11, in_14}), .in_3({undriven_9, in_13}), .in_5({undriven_7, in_12}),
    .out_8(undriven_11[1]));  // open: in_4, in_6, in_7
endmodule

module LUT_v2 (
  input  [7:0] in_1,
  input  in_2,
  input  in_3,
  input  in_4,
  output out_5
);

  Multiplexer #(.select(3), .enable("false")) multiplexer_1 (
    .in0(in_1[0]), .in1(in_1[1]), .in2(in_1[2]), .in3(in_1[3]), .in4(in_1[4]), .in5(in_1[5]), .in6(in_1[6]),
    .in7(in_1[7]), .out(out_5), .sel({in_2, in_3, in_4}));
endmodule

module Switch_matrix (
  input  in_1,
  input  in_2,
  input  in_3,
  input  in_4,
  input  in_5,
  input  in_6,
  input  in_7,
  input  [2:0] in_8,
  output out_9
);

  Multiplexer #(.select(3), .enable("false")) multiplexer_1 (
    .in0(in_1), .in1(in_2), .in2(in_3), .in3(in_4), .in4(in_5), .in5(in_6), .in6(in_7), .out(out_9),
    .sel(in_8));  // open: in7
endmodule

module lut_switch (
  input  [7:0] in_1,
  input  [7:0] in_2,
  input  [7:0] in_3,
  input  [2:0] in_4,
  input  [7:0] in_5,
  input  [2:0] in_6,
  input  [2:0] in_7,
  output out_8
);

  wire switch_matrix_1_out_9, switch_matrix_2_out_9, switch_matrix_3_out_9;

  Switch_matrix switch_matrix_1 (
    .in_1(in_2[0]), .in_2(in_2[1]), .in_3(in_2[2]), .in_4(in_2[3]), .in_5(in_2[4]), .in_6(in_2[5]),
    .in_7(in_2[6]), .in_8(in_7), .out_9(switch_matrix_1_out_9));
  Switch_matrix switch_matrix_2 (
    .in_1(in_3[0]), .in_2(in_3[1]), .in_3(in_3[2]), .in_4(in_3[3]), .in_5(in_3[4]), .in_6(in_3[5]),
    .in_7(in_3[6]), .in_8(in_6), .out_9(switch_matrix_2_out_9));
  Switch_matrix switch_matrix_3 (
    .in_1(in_5[0]), .in_2(in_5[1]), .in_3(in_5[2]), .in_4(in_5[3]), .in_5(in_5[4]), .in_6(in_5[5]),
    .in_7(in_5[6]), .in_8(in_4), .out_9(switch_matrix_3_out_9));
  LUT_v2 lut_v2_1 (
    .in_1(in_1), .in_2(switch_matrix_1_out_9), .in_3(switch_matrix_2_out_9), .in_4(switch_matrix_3_out_9),
    .out_5(out_8));
endmodule
